// Logisim project HK8.circ as structural Verilog: 4 circuits, main circuit main
module main (
);

  wire button_1_out, sys_clock_1_clk, sys_clock_1_not_clk;

  Button button_1 (.out(button_1_out));
  Sys_CLock sys_clock_1 (.HALT(button_1_out), .CLK(sys_clock_1_clk), .NOT_CLK(sys_clock_1_not_clk));
  LED led_1 (.in(sys_clock_1_clk));
  LED led_2 (.in(sys_clock_1_not_clk));
endmodule

module Sys_CLock (
  input  HALT,
  output CLK,
  output NOT_CLK
);

  wire clock_1_out, not_2_out;

  not not_1 (NOT_CLK, CLK);
  and and_1 (CLK, clock_1_out, not_2_out);
  Clock clock_1 (.out(clock_1_out));
  not not_2 (not_2_out, HALT);
endmodule

module Output_8_bit (
  input  OUTI,
  input  B0,
  input  B1,
  input  B2,
  input  B3,
  input  B4,
  input  B5,
  input  B6,
  input  B7
);

  _7_Segment_Display u_7_segment_display_1 ();  // open: g, f, a, b, e, d, c, dp
  _7_Segment_Display u_7_segment_display_2 ();  // open: g, f, a, b, e, d, c, dp
  _7_Segment_Display u_7_segment_display_3 ();  // open: g, f, a, b, e, d, c, dp
  _7_Segment_Display u_7_segment_display_4 ();  // open: g, f, a, b, e, d, c, dp
endmodule

module REG_8B (
  input  STR,
  input  OT,
  input  IN0,
  input  IN1,
  input  IN2,
  input  IN3,
  input  IN4,
  input  IN5,
  input  IN6,
  input  IN7,
  output B0,
  output B1,
  output B2,
  output B3,
  output B4,
  output B5,
  output B6,
  output B7
);

  Register register_1 ();  // open: D, en, clk, Q, clr
endmodule
